// Logisim project proba2.circ as structural Verilog: 3 circuits, main circuit main
module main (
);

  wire _32_out, _64_out, _128_out, _256_out, comparator_1_eq, controlled_buffer_1_out, ending,
       keyboard_1_avail, main_1_p5, main_1_p6, main_1_p7, main_1_p8, main_2_p3, main_2_p4, main_2_p5,
       main_2_p6, main_3_p2, main_3_p4, main_3_p6, main_3_p8, main_3_p10, main_3_p12, main_3_p14, main_3_p17,
       main_3_p19, main_3_p21, main_3_p23, main_4_p2, main_4_p4, main_4_p6, main_4_p8, not_1_out,
       register_1_q, reset, \reset_lub_wciśnij_klawisz_r_out , \skok_lub_wciśnij_spacje_out ,
       \音乐播放器_1_enable ;
  wire [6:0] keyboard_1_data;
  wire [13:0] \音乐播放器_1_out_5 ;
  wire [31:0] main_4_p10, main_4_p11, main_4_p12, main_4_p13, main_4_p14, main_4_p15, main_4_p16, main_4_p17,
       main_4_p18, main_4_p19, main_4_p20, main_4_p21, main_4_p22, main_4_p23, main_4_p24, main_4_p25;

  Clock #(.highDuration(8), .lowDuration(8)) _32 (.out(_32_out));
  Clock #(.highDuration(4), .lowDuration(4)) _64 (.out(_64_out));
  Clock #(.highDuration(2), .lowDuration(2)) _128 (.out(_128_out));
  Clock #(.highDuration(1), .lowDuration(1)) _256 (.out(_256_out));
  // clock_zmiana_main main_1: pin names not known; wires that end beside it: _32_out, _64_out, _128_out, _256_out, main_1_p5, main_1_p6, main_1_p7, main_1_p8
  // mały_lub_duży_main main_2: pin names not known; wires that end beside it: main_1_p8, ending, main_2_p3, main_2_p4, main_2_p5, main_2_p6, ending, main_1_p8, main_2_p4, main_2_p3
  assign controlled_buffer_1_out = keyboard_1_avail ? main_1_p8 : 1'bz;  // Controlled_Buffer controlled_buffer_1
  not not_1 (not_1_out, ending);
  Keyboard #(.Char_bit_width(7), .buflen(32), .trigger("rising")) keyboard_1 (
    .clk(controlled_buffer_1_out), .avail(keyboard_1_avail), .data(keyboard_1_data));  // open: re, clr
  // przegrana_main main_3: pin names not known; wires that end beside it: main_2_p5, main_3_p2, main_3_p2, main_3_p4, main_3_p4, main_3_p6, main_3_p6, main_3_p8, main_3_p8, main_3_p10, main_3_p10, main_3_p12, main_3_p12, main_3_p14, main_3_p14, ending, main_3_p17, main_3_p17, main_3_p19, main_3_p19, main_3_p21, main_3_p21, main_3_p23
  Register #(.width(1), .trigger("rising"), .Select("low")) register_1 (
    .D(not_1_out), .Q(register_1_q), .clk(_128_out));  // open: en, clr
  // DotMatrix #(.inputtype("column"), .matrixcols(32), .matrixrows(16), .persist(0), .dotshape("square")) dotmatrix_1: pin names not known; wires that end beside it: _32_out, ending, main_2_p5, main_1_p5, main_1_p6
  DotMatrix #(.inputtype("row"), .matrixcols(32), .matrixrows(16), .persist(0), .dotshape("square")) dotmatrix_2 (
    .row0(main_4_p10), .row1(main_4_p11), .row2(main_4_p12), .row3(main_4_p13), .row4(main_4_p14),
    .row5(main_4_p15), .row6(main_4_p16), .row7(main_4_p17), .row8(main_4_p18), .row9(main_4_p19),
    .row10(main_4_p20), .row11(main_4_p21), .row12(main_4_p22), .row13(main_4_p23), .row14(main_4_p24),
    .row15(main_4_p25));
  // skroceniev2_led_main main_4: pin names not known; wires that end beside it: main_3_p23, main_4_p2, main_4_p2, main_4_p4, main_4_p4, main_4_p6, main_4_p6, main_4_p8, main_4_p8, main_4_p10, main_4_p11, main_4_p12, main_4_p13, main_4_p14, main_4_p15, main_4_p16, main_4_p17, main_4_p18, main_4_p19, main_4_p20, main_4_p21, main_4_p22, main_4_p23, main_4_p24, main_4_p25
  \音乐播放器  \u_音乐播放器_1  (
    .\频率延缓倍数 (16'h2), .CLK(_128_out), .play(register_1_q), .RST(reset), .out_5(\音乐播放器_1_out_5 ),
    .Enable(\音乐播放器_1_enable ));  // open: out_7
  Button \reset_lub_wciśnij_klawisz_r  (.out(\reset_lub_wciśnij_klawisz_r_out ));
  Comparator #(.width(7), .mode("twosComplement")) comparator_1 (
    .a(keyboard_1_data), .b(7'b0100000), .eq(comparator_1_eq));  // open: gt, lt
  Comparator #(.width(7), .mode("twosComplement")) comparator_2 (
    .a(keyboard_1_data), .b(7'b1110010), .eq(reset));  // open: gt, lt
  // Buzzer #(.freq_measure("Hz"), .vol_width(7)) buzzer_1: pin names not known; wires that end beside it: \音乐播放器_1_out_5 , \音乐播放器_1_enable , 7'b0010100
  or or_1 (main_2_p5, \reset_lub_wciśnij_klawisz_r_out , reset);
  or or_2 (main_2_p6, comparator_1_eq, \skok_lub_wciśnij_spacje_out );
  Button \skok_lub_wciśnij_spacje  (.out(\skok_lub_wciśnij_spacje_out ));
  // wynik_wyświetlanie_duży_main main_5: pin names not known; wires that end beside it: main_1_p7
endmodule

module \频率转换器  (
  input  [15:0] \延缓倍数 ,
  input  \原CLK ,
  input  RST,
  output \后CLK 
);

  wire comparator_1_eq, comparator_2_eq, comparator_2_gt, or_1_out;
  wire [15:0] counter_1_q, shifter_1_out;

  Shifter #(.width(16), .shift("lr")) shifter_1 (.in(\延缓倍数 ), .\dist (4'b0001), .out(shifter_1_out));
  Counter #(.width(16), .max('hffff), .ongoal("wrap"), .trigger("rising"), .behavior("new")) counter_1 (
    .load(comparator_1_eq), .D({16{1'b0}}), .Q(counter_1_q), .clk(\原CLK ), .clr(RST));  // open: count, carry, preset, down
  Comparator #(.width(16), .mode("unsigned")) comparator_1 (
    .a(\延缓倍数 ), .b(counter_1_q), .eq(comparator_1_eq));  // open: gt, lt
  Comparator #(.width(16), .mode("unsigned")) comparator_2 (
    .a(shifter_1_out), .b(counter_1_q), .gt(comparator_2_gt), .eq(comparator_2_eq));  // open: lt
  or or_1 (or_1_out, comparator_2_gt, comparator_2_eq);
  Multiplexer #(.select(1), .width(1), .disabled("Z"), .enable("false")) multiplexer_1 (
    .in0(1'b1), .in1(1'b0), .out(\后CLK ), .sel(or_1_out));
endmodule

module \音乐播放器  (
  input  [15:0] \频率延缓倍数 ,
  input  CLK,
  input  play,
  input  RST,
  output [13:0] out_5,
  output Enable,
  output [13:0] out_7
);

  wire Now_CLK;
  wire [31:0] adder_1_out, PC_q;
  wire [31:14] \主_data , \伴奏_data ;

  Register #(.width(32), .trigger("rising"), .Select("low")) PC (
    .D(adder_1_out), .en(play), .Q(PC_q), .clk(Now_CLK), .clr(RST));
  \频率转换器  \u_频率转换器_1  (.\延缓倍数 (\频率延缓倍数 ), .\原CLK (CLK), .RST(RST), .\后CLK (Now_CLK));
  Adder #(.width(32)) adder_1 (.a(PC_q), .b(32'h4), .out(adder_1_out), .cout(RST));  // open: cin
  ROM #(.addrWidth(10), .dataWidth(32), .Select("high")) \u_主  (.addr(PC_q[11:2]), .data({\主_data , out_5}));
  ROM #(.addrWidth(10), .dataWidth(32), .Select("high")) \u_伴奏  (.addr(PC_q[11:2]), .data({\伴奏_data , out_7}));

  assign Enable = play;

  // Notes on the sheet:
  //   建议频率:转换后：16Hz
  //   contents of 主 (hex, n*v repeats v):
  //   20b 20b 20b 0 20b 20b 20b 0 310 310 310 0 310 310 310 0 370 370 370 0 370 370 370 0 310 310 310 5*0
  //   2ba 2ba 2ba 0 2ba 2ba 2ba 0 293 293 293 0 293 293 293 0 24b 24b 24b 0 24b 24b 24b 0 20b 20b 20b 5*0
  //   310 310 310 0 310 310 310 0 2ba 2ba 2ba 0 2ba 2ba 2ba 0 293 293 293 0 293 293 293 0 24b 24b 24b 5*0
  //   310 310 310 0 310 310 310 0 2ba 2ba 2ba 0 2ba 2ba 2ba 0 293 293 293 0 293 293 293 0 24b 24b 24b 5*0
  //   20b 20b 20b 0 20b 20b 20b 0 310 310 310 0 310 310 310 0 370 370 370 0 370 370 370 0 310 310 310 5*0
  //   2ba 2ba 2ba 0 2ba 2ba 2ba 0 293 293 293 0 293 293 293 0 24b 24b 24b 0 24b 24b 24b 0 6*20b 0 20b 20b
  //   20b 0 310 310 310 0 310 310 310 0 370 370 370 0 370 370 370 0 310 310 310 5*0 2ba 2ba 2ba 0 2ba 2ba
  //   2ba 0 293 293 293 0 293 293 293 0 24b 24b 24b 0 24b 24b 24b 0 20b 20b 20b 5*0 310 310 310 0 310 310
  //   310 0 2ba 2ba 2ba 0 2ba 2ba 2ba 0 293 293 293 0 293 293 293 0 24b 24b 24b 5*0 310 310 310 0 310 310
  //   310 0 2ba 2ba 2ba 0 2ba 2ba 2ba 0 293 293 293 0 293 293 293 0 24b 24b 24b 5*0 20b 20b 20b 0 20b 20b
  //   20b 0 310 310 310 0 310 310 310 0 370 370 370 0 370 370 370 0 310 310 310 5*0 2ba 2ba 2ba 0 2ba 2ba
  //   2ba 0 293 293 293 0 293 293 293 0 24b 24b 24b 0 24b 24b 24b 0 6*20b 0 20b 20b 20b 0 310 310 310 0
  //   310 310 310 0 370 370 370 0 370 370 370 0 310 310 310 5*0 2ba 2ba 2ba 0 2ba 2ba 2ba 0 293 293 293 0
  //   293 293 293 0 24b 24b 24b 0 24b 24b 24b 0 20b 20b 20b 5*0 310 310 310 0 310 310 310 0 2ba 2ba 2ba 0
  //   2ba 2ba 2ba 0 293 293 293 0 293 293 293 0 24b 24b 24b 5*0 310 310 310 0 310 310 310 0 2ba 2ba 2ba 0
  //   2ba 2ba 2ba 0 293 293 293 0 293 293 293 0 24b 24b 24b 5*0 20b 20b 20b 0 20b 20b 20b 0 310 310 310 0
  //   310 310 310 0 370 370 370 0 370 370 370 0 310 310 310 5*0 2ba 2ba 2ba 0 2ba 2ba 2ba 0 293 293 293 0
  //   293 293 293 0 24b 24b 24b 0 20b 20b 20b 0 20b 20b 20b 0 310 310 310 0 310 310 310 0 370 370 370 0
  //   370 370 370 0 310 310 310 5*0 2ba 2ba 2ba 0 2ba 2ba 2ba 0 293 293 293 0 293 293 293 0 24b 24b 24b 0
  //   24b 24b 24b 0 20b 20b 20b 5*0 310 310 310 0 310 310 310 0 2ba 2ba 2ba 0 2ba 2ba 2ba 0 293 293 293 0
  //   293 293 293 0 24b 24b 24b 5*0 310 310 310 0 310 310 310 0 2ba 2ba 2ba 0 2ba 2ba 2ba 0 293 293 293 0
  //   293 293 293 0 24b 24b 24b 5*0 20b 20b 20b 0 20b 20b 20b 0 310 310 310 0 310 310 310 0 370 370 370 0
  //   370 370 370 0 310 310 310 5*0 2ba 2ba 2ba 0 2ba 2ba 2ba 0 293 293 293 0 293 293 293 0 24b 24b 24b 0
  //   24b 24b 24b 0 6*20b 0 20b 20b 20b 0 310 310 310 0 310 310 310 0 370 370 370 0 370 370 370 0 310 310
  //   310 5*0 2ba 2ba 2ba 0 2ba 2ba 2ba 0 293 293 293 0 293 293 293 0 24b 24b 24b 0 24b 24b 24b 0 20b 20b
  //   20b 5*0 310 310 310 0 310 310 310 0 2ba 2ba 2ba 0 2ba 2ba 2ba 0 293 293 293 0 293 293 293 0 24b 24b
  //   24b 5*0 310 310 310 0 310 310 310 0 2ba 2ba 2ba 0 2ba 2ba 2ba 0 293 293 293 0 293 293 293 0 24b 24b
  //   24b 5*0 20b 20b 20b 0 20b 20b 20b 0 310 310 310 0 310 310 310 0 370 370 370 0 370 370 370 0 310 310
  //   310 5*0 2ba 2ba 2ba 0 2ba 2ba 2ba 0 293 293 293 0 293 293 293 0 24b 24b 24b 0 24b 24b 24b 0 20b 20b
  //   20b 24b 24b 24b 0 20b 20b 20b
  //   contents of 伴奏 (hex, n*v repeats v):
  //   106 106 188 188 14a 14a 188 188 106 106 188 188 14a 14a 188 188 106 106 1b8 1b8 15d 15d 1b8 1b8 106
  //   106 188 188 14a 14a 188 188 e9 e9 188 188 126 126 188 188 106 106 188 188 14a 14a 188 188 e9 e9 188
  //   188 126 126 188 188 106 106 188 188 14a 14a 188 188 106 106 188 188 14a 14a 188 188 e9 e9 188 188
  //   126 126 188 188 106 106 188 188 14a 14a 188 188 e9 e9 188 188 126 126 188 188 106 106 188 188 14a
  //   14a 188 188 e9 e9 188 188 126 126 188 188 106 106 188 188 14a 14a 188 188 e9 e9 188 188 126 126 188
  //   188 106 106 188 188 14a 14a 188 188 106 106 188 188 14a 14a 188 188 106 106 1b8 1b8 15d 15d 1b8 1b8
  //   106 106 188 188 14a 14a 188 188 e9 e9 188 188 126 126 188 188 106 106 188 188 14a 14a 188 188 e9 e9
  //   188 188 126 126 188 188 106 106 188 188 14a 14a 188 188
  //   小星星变奏曲-前奏
endmodule
